// Logisim project ALU.circ as structural Verilog: 13 circuits, main circuit or_4bits
module ALU_2 (
  input  A0__MSB,
  input  A1,
  input  A2,
  input  A3,
  input  B0__MSB,
  input  B1,
  input  B2,
  input  B3,
  input  [2:0] in_9,
  output out_10
);

  wire AN0, AN1, AN2, AN3, AND, and_1_out, and_2_out, and_3_out, and_4_out, and_4bits_1_lsb_3,
       and_4bits_1_msb_3, and_4bits_1_out_10, and_4bits_1_out_11, and_5_out, and_6_out, and_7_out, and_8_out,
       and_9_out, and_10_out, and_11_out, and_12_out, and_13_out, and_14_out, and_15_out, and_16_out,
       and_21_out, and_22_out, and_23_out, and_24_out, and_25_out, and_26_out, and_27_out, and_28_out,
       and_29_out, and_30_out, and_31_out, and_32_out, and_33_out, and_34_out, and_35_out, and_36_out,
       and_44_out, and_45_out, and_46_out, and_47_out, and_48_out, and_49_out, and_50_out, and_51_out,
       and_52_out, and_53_out, and_54_out, and_55_out, and_56_out, and_57_out, and_58_out, and_59_out,
       bcd_7segmentos_derecha_1_a, bcd_7segmentos_derecha_1_b, bcd_7segmentos_derecha_1_c,
       bcd_7segmentos_derecha_1_d, bcd_7segmentos_derecha_1_e, bcd_7segmentos_derecha_1_f,
       bcd_7segmentos_derecha_1_g, bcd_7segmentos_izquierda_1_a, bcd_7segmentos_izquierda_1_b,
       bcd_7segmentos_izquierda_1_c, bcd_7segmentos_izquierda_1_d, bcd_7segmentos_izquierda_1_e,
       bcd_7segmentos_izquierda_1_f, bcd_7segmentos_izquierda_1_g, c0, c1, c2, c3, c4,
       comparador_4bits_otm_1_igual, comparador_4bits_otm_1_mayor, comparador_4bits_otm_1_menor,
       COMPARADORES, d0, d1, d2, d3, IGUAL, MAYOR, MENOR, NO0, NO1, NO2, NO3, NOT, not_4bits_1_out_5,
       not_4bits_1_out_6, not_4bits_1_out_7, not_4bits_1_out_8, O0, O1, O2, O3, OR, or_4bits_1_a0_2,
       or_4bits_1_a1_2, or_4bits_1_a2_2, or_4bits_1_a3_2, or_9_out, or_10_out, or_11_out, or_12_out, r0, r1,
       r2, r3, RESTA, rs, S0, S1, S2, S3, SUMA, XO0, XO1, XO2, XO3, XOR, xor_4bits_1_lsb_3,
       xor_4bits_1_msb_3, xor_4bits_1_out_10, xor_4bits_1_out_11;

  Demultiplexer #(.select(3)) demultiplexer_1 (
    .out0(SUMA), .out1(RESTA), .out2(AND), .out3(OR), .out4(XOR), .out5(NOT), .out6(COMPARADORES), .in(1'b1),
    .sel(in_9));  // open: out7, en
  LED led_1 (.in(d3));
  or or_1 (d0, AN0, O0, XO0, NO0);
  not not_1 (out_10, rs);
  _7_Segment_Display u_7_segment_display_1 (.g(out_10));  // open: f, a, b, e, d, c, dp
  LED led_2 (.in(d2));
  LED led_3 (.in(d1));
  LED led_4 (.in(d0));
  _7_Segment_Display u_7_segment_display_2 (
    .g(bcd_7segmentos_izquierda_1_g), .f(bcd_7segmentos_izquierda_1_f), .a(bcd_7segmentos_izquierda_1_a),
    .b(bcd_7segmentos_izquierda_1_b), .e(bcd_7segmentos_izquierda_1_e), .d(bcd_7segmentos_izquierda_1_d),
    .c(bcd_7segmentos_izquierda_1_c));  // open: dp
  BCD_7SEGMENTOS_IZQUIERDA bcd_7segmentos_izquierda_1 (
    .d(bcd_7segmentos_izquierda_1_d), .g(bcd_7segmentos_izquierda_1_g), .b(bcd_7segmentos_izquierda_1_b),
    .e(bcd_7segmentos_izquierda_1_e), .a(bcd_7segmentos_izquierda_1_a), .c(bcd_7segmentos_izquierda_1_c),
    .f(bcd_7segmentos_izquierda_1_f), .A4(c4), .A3(c3), .A2(c2), .A1(c1), .A0(c0));
  or or_2 (c0, S0, r0);
  or or_3 (c1, S1, r1);
  or or_4 (d1, AN1, O1, XO1, NO1);
  or or_5 (c2, S2, r2);
  BCD_7SEGMENTOS_DERECHA bcd_7segmentos_derecha_1 (
    .x0(c0), .x1(c1), .x2(c2), .x3(c3), .x4(c4), .a(bcd_7segmentos_derecha_1_a),
    .b(bcd_7segmentos_derecha_1_b), .c(bcd_7segmentos_derecha_1_c), .d(bcd_7segmentos_derecha_1_d),
    .e(bcd_7segmentos_derecha_1_e), .f(bcd_7segmentos_derecha_1_f), .g(bcd_7segmentos_derecha_1_g));
  LED led_5 (.in(IGUAL));
  or or_6 (c3, S3, r3);
  _7_Segment_Display u_7_segment_display_3 (
    .g(bcd_7segmentos_derecha_1_g), .f(bcd_7segmentos_derecha_1_f), .a(bcd_7segmentos_derecha_1_a),
    .b(bcd_7segmentos_derecha_1_b), .e(bcd_7segmentos_derecha_1_e), .d(bcd_7segmentos_derecha_1_d),
    .c(bcd_7segmentos_derecha_1_c));  // open: dp
  LED led_6 (.in(MAYOR));
  LED led_7 (.in(MENOR));
  or or_7 (d2, AN2, O2, XO2, NO2);
  or or_8 (d3, AN3, O3, XO3, NO3);
  and and_1 (and_1_out, A0__MSB, OR);
  and and_2 (and_2_out, A1, OR);
  and and_3 (and_3_out, A2, OR);
  and and_4 (and_4_out, A3, OR);
  and and_5 (and_5_out, B0__MSB, OR);
  and and_6 (and_6_out, B1, OR);
  and and_7 (and_7_out, B2, OR);
  and and_8 (and_8_out, B3, OR);
  and and_9 (and_9_out, A0__MSB, SUMA);
  and and_10 (and_10_out, A1, SUMA);
  and and_11 (and_11_out, A2, SUMA);
  and and_12 (and_12_out, A3, SUMA);
  and and_13 (and_13_out, B0__MSB, SUMA);
  and and_14 (and_14_out, B1, SUMA);
  and and_15 (and_15_out, B2, SUMA);
  and and_16 (and_16_out, B3, SUMA);
  or_4bits or_4bits_1 (
    .A3(and_1_out), .A2(and_2_out), .A1(and_3_out), .A0(and_4_out), .B3(and_5_out), .B2(and_6_out),
    .B1(and_7_out), .B0(and_8_out), .A3_2(or_4bits_1_a3_2), .A2_2(or_4bits_1_a2_2), .A1_2(or_4bits_1_a1_2),
    .A0_2(or_4bits_1_a0_2));
  and and_17 (O3, OR, or_4bits_1_a3_2);
  and and_18 (O2, OR, or_4bits_1_a2_2);
  and and_19 (O1, or_4bits_1_a1_2, OR);
  and and_20 (O0, or_4bits_1_a0_2, OR);
  sumador_4bits sumador_4bits_1 (
    .A3(and_9_out), .A2(and_10_out), .A1(and_11_out), .A0(and_12_out), .B3(and_13_out), .B2(and_14_out),
    .B1(and_15_out), .B0(and_16_out), .Carry_in(1'b0), .Carry(c4), .S3(S3), .S2(S2), .S1(S1), .S0(S0));
  and and_21 (and_21_out, A0__MSB, RESTA);
  and and_22 (and_22_out, A1, RESTA);
  and and_23 (and_23_out, A2, RESTA);
  and and_24 (and_24_out, A3, RESTA);
  and and_25 (and_25_out, B0__MSB, RESTA);
  and and_26 (and_26_out, B1, RESTA);
  and and_27 (and_27_out, B2, RESTA);
  and and_28 (and_28_out, B3, RESTA);
  and and_29 (and_29_out, A0__MSB, XOR);
  and and_30 (and_30_out, A1, XOR);
  and and_31 (and_31_out, A2, XOR);
  and and_32 (and_32_out, A3, XOR);
  and and_33 (and_33_out, B0__MSB, XOR);
  and and_34 (and_34_out, B1, XOR);
  and and_35 (and_35_out, B2, XOR);
  and and_36 (and_36_out, B3, XOR);
  comparador_4bits_otm comparador_4bits_otm_1 (
    .A3(A0__MSB), .A2(A1), .A1(A2), .A0(A3), .B3(B0__MSB), .B2(B1), .B1(B2), .B0(B3),
    .Igual(comparador_4bits_otm_1_igual), .Mayor(comparador_4bits_otm_1_mayor),
    .Menor(comparador_4bits_otm_1_menor));
  restador_4bits restador_4bits_1 (
    .A3(and_21_out), .A2(and_22_out), .A1(and_23_out), .A0(and_24_out), .B3(and_25_out), .B2(and_26_out),
    .B1(and_27_out), .B0(and_28_out), .SIGNO(rs), .S4(r3), .S3(r2), .S2(r1), .S1(r0));
  XOR_4bits xor_4bits_1 (
    .MSB(and_29_out), .A(and_30_out), .in_3(and_31_out), .LSB(and_32_out), .MSB_2(and_33_out),
    .B(and_34_out), .in_7(and_35_out), .LSB_2(and_36_out), .MSB_3(xor_4bits_1_msb_3),
    .out_10(xor_4bits_1_out_10), .out_11(xor_4bits_1_out_11), .LSB_3(xor_4bits_1_lsb_3));
  and and_37 (IGUAL, comparador_4bits_otm_1_igual, COMPARADORES);
  and and_38 (MAYOR, comparador_4bits_otm_1_mayor, COMPARADORES);
  and and_39 (MENOR, comparador_4bits_otm_1_menor, COMPARADORES);
  and and_40 (XO3, XOR, xor_4bits_1_msb_3);
  and and_41 (XO2, XOR, xor_4bits_1_out_10);
  and and_42 (XO1, xor_4bits_1_out_11, XOR);
  and and_43 (XO0, xor_4bits_1_lsb_3, XOR);
  and and_44 (and_44_out, A0__MSB, AND);
  and and_45 (and_45_out, A1, AND);
  and and_46 (and_46_out, A2, AND);
  and and_47 (and_47_out, A3, AND);
  and and_48 (and_48_out, B0__MSB, AND);
  and and_49 (and_49_out, B1, AND);
  and and_50 (and_50_out, B2, AND);
  and and_51 (and_51_out, B3, AND);
  and and_52 (and_52_out, A0__MSB, NOT);
  and and_53 (and_53_out, A1, NOT);
  and and_54 (and_54_out, A2, NOT);
  and and_55 (and_55_out, A3, NOT);
  and and_56 (and_56_out, B0__MSB, NOT);
  and and_57 (and_57_out, B1, NOT);
  and and_58 (and_58_out, B2, NOT);
  and and_59 (and_59_out, B3, NOT);
  AND_4bits and_4bits_1 (
    .MSB(and_44_out), .A(and_45_out), .in_3(and_46_out), .LSB(and_47_out), .MSB_2(and_48_out),
    .B(and_49_out), .in_7(and_50_out), .LSB_2(and_51_out), .MSB_3(and_4bits_1_msb_3),
    .out_10(and_4bits_1_out_10), .out_11(and_4bits_1_out_11), .LSB_3(and_4bits_1_lsb_3));
  and and_60 (AN3, AND, and_4bits_1_msb_3);
  and and_61 (AN2, AND, and_4bits_1_out_10);
  and and_62 (AN1, and_4bits_1_out_11, AND);
  and and_63 (AN0, and_4bits_1_lsb_3, AND);
  or or_9 (or_9_out, and_52_out, and_56_out);
  or or_10 (or_10_out, and_53_out, and_57_out);
  or or_11 (or_11_out, and_58_out, and_54_out);
  or or_12 (or_12_out, and_55_out, and_59_out);
  not_4bits not_4bits_1 (
    .in_1(or_9_out), .in_2(or_10_out), .in_3(or_11_out), .in_4(or_12_out), .out_5(not_4bits_1_out_5),
    .out_6(not_4bits_1_out_6), .out_7(not_4bits_1_out_7), .out_8(not_4bits_1_out_8));
  and and_64 (NO3, NOT, not_4bits_1_out_5);
  and and_65 (NO2, NOT, not_4bits_1_out_6);
  and and_66 (NO1, not_4bits_1_out_7, NOT);
  and and_67 (NO0, not_4bits_1_out_8, NOT);

  // Other names for the same wires on the sheet: A0 = A0__MSB; B0 = B0__MSB; S4 = c4

  // Notes on the sheet:
  //   000 -> SUMA
  //   001 --> RESTA
  //   010 --> AND
  //   011 --> OR
  //   100 --> XOR
  //   101 --> NOT
  //   110 --> COMPARADORES
  //   (PARA EL NOT, SE DEBE MANTENER EN 0
  //   EL NUMERO QUE NO SE QUIERE MOSTRAR)
  //   (Mantener apagado el que no se va a negar)
  //   SALIDAS PARA AND, OR, XOR Y NOT
  //   Invertidos porque en las salida individuales estaban invertdos
  //   PARA ESCOGER ENTRE AND, OR, XOR, NOT
  //   PARA ESCOGER SI ES SUMA O RESTA (SE MUESTRA EN LOS 2 DISPLAYS)
  //   A <>= B
endmodule

module sumador_4bits (
  input  A3,
  input  A2,
  input  A1,
  input  A0,
  input  B3,
  input  B2,
  input  B1,
  input  B0,
  input  Carry_in,
  output Carry,
  output S3,
  output S2,
  output S1,
  output S0
);

  wire sumador_1bit_2_carryout, sumador_1bit_3_carryout, sumador_1bit_4_carryout;

  sumador_1bit sumador_1bit_1 (.A(A3), .B(B3), .Cin(sumador_1bit_2_carryout), .Suma(S3), .CarryOut(Carry));
  sumador_1bit sumador_1bit_2 (
    .A(A2), .B(B2), .Cin(sumador_1bit_3_carryout), .Suma(S2), .CarryOut(sumador_1bit_2_carryout));
  sumador_1bit sumador_1bit_3 (
    .A(A1), .B(B1), .Cin(sumador_1bit_4_carryout), .Suma(S1), .CarryOut(sumador_1bit_3_carryout));
  sumador_1bit sumador_1bit_4 (.A(A0), .B(B0), .Cin(Carry_in), .Suma(S0), .CarryOut(sumador_1bit_4_carryout));

  // Notes on the sheet:
  //   A
  //   B
endmodule

module sumador_1bit (
  input  A,
  input  B,
  input  Cin,
  output Suma,
  output CarryOut
);

  wire and_1_out, and_2_out, xor_1_out;

  xor xor_1 (xor_1_out, A, B);
  and and_1 (and_1_out, xor_1_out, Cin);
  and and_2 (and_2_out, A, B);
  xor xor_2 (Suma, xor_1_out, Cin);
  or or_1 (CarryOut, and_1_out, and_2_out);
endmodule

module restador_4bits (
  input  A3,
  input  A2,
  input  A1,
  input  A0,
  input  B3,
  input  B2,
  input  B1,
  input  B0,
  output SIGNO,
  output S4,
  output S3,
  output S2,
  output S1
);

  wire and_1_out, and_2_out, and_3_out, and_4_out, and_5_out, and_6_out, and_7_out, and_8_out, cs1, cs2, cs3,
       cs4, not_1_out, not_2_out, not_3_out, not_4_out, not_5_out, restador_1bit_2_carry_out,
       restador_1bit_3_carry_out, restador_1bit_4_carry_out, s0, s1_t, s2_t, s3_t;

  restador_1bit restador_1bit_1 (.A(A3), .B(B3), .Cin(restador_1bit_2_carry_out), .Salida(s3_t), .Carry_out(SIGNO));
  restador_1bit restador_1bit_2 (
    .A(A2), .B(B2), .Cin(restador_1bit_3_carry_out), .Salida(s2_t), .Carry_out(restador_1bit_2_carry_out));
  restador_1bit restador_1bit_3 (
    .A(A1), .B(B1), .Cin(restador_1bit_4_carry_out), .Salida(s1_t), .Carry_out(restador_1bit_3_carry_out));
  restador_1bit restador_1bit_4 (.A(A0), .B(B0), .Cin(1'b1), .Salida(s0), .Carry_out(restador_1bit_4_carry_out));
  not not_1 (not_1_out, s3_t);
  not not_2 (not_2_out, s2_t);
  not not_3 (not_3_out, s1_t);
  not not_4 (not_4_out, s0);
  sumador_4bits sumador_4bits_1 (
    .A3(not_1_out), .A2(not_2_out), .A1(not_3_out), .A0(not_4_out), .B3(1'b0), .B2(1'b0), .B1(1'b0),
    .B0(1'b1), .Carry_in(1'b0), .S3(cs4), .S2(cs3), .S1(cs2), .S0(cs1));  // open: Carry
  and and_1 (and_1_out, s3_t, SIGNO);
  and and_2 (and_2_out, s2_t, SIGNO);
  and and_3 (and_3_out, s1_t, SIGNO);
  and and_4 (and_4_out, s0, SIGNO);
  not not_5 (not_5_out, SIGNO);
  and and_5 (and_5_out, cs4, not_5_out);
  and and_6 (and_6_out, cs3, not_5_out);
  and and_7 (and_7_out, cs2, not_5_out);
  and and_8 (and_8_out, cs1, not_5_out);
  or or_1 (S4, and_1_out, and_5_out);
  or or_2 (S3, and_2_out, and_6_out);
  or or_3 (S2, and_3_out, and_7_out);
  or or_4 (S1, and_4_out, and_8_out);

  // Other names for the same wires on the sheet: T_signo = SIGNO

  // Notes on the sheet:
  //   1 ES POSITIVO
  //   0 ES NEGATIVO
endmodule

module restador_1bit (
  input  A,
  input  B,
  input  Cin,
  output Salida,
  output Carry_out
);

  wire and_1_out, and_2_out, xor_1_out;

  xor xor_1 (xor_1_out, A, ~B);  // XOR_Gate
  and and_1 (and_1_out, xor_1_out, Cin);
  and and_2 (and_2_out, A, ~B);  // AND_Gate
  xor xor_2 (Salida, xor_1_out, Cin);
  or or_1 (Carry_out, and_1_out, and_2_out);

  // Notes on the sheet:
  //   FIJAR EN 1
endmodule

module AND_4bits (
  input  MSB,
  input  A,
  input  in_3,
  input  LSB,
  input  MSB_2,
  input  B,
  input  in_7,
  input  LSB_2,
  output MSB_3,
  output out_10,
  output out_11,
  output LSB_3
);

  and and_1 (MSB_3, MSB, MSB_2);
  and and_2 (out_10, A, B);
  and and_3 (out_11, in_3, in_7);
  and and_4 (LSB_3, LSB, LSB_2);
endmodule

module or_4bits (
  input  A3,
  input  A2,
  input  A1,
  input  A0,
  input  B3,
  input  B2,
  input  B1,
  input  B0,
  output A3_2,
  output A2_2,
  output A1_2,
  output A0_2
);

  or or_1 (A3_2, A3, B3);
  or or_2 (A2_2, A2, B2);
  or or_3 (A1_2, A1, B1);
  or or_4 (A0_2, A0, B0);
endmodule

module XOR_4bits (
  input  MSB,
  input  A,
  input  in_3,
  input  LSB,
  input  MSB_2,
  input  B,
  input  in_7,
  input  LSB_2,
  output MSB_3,
  output out_10,
  output out_11,
  output LSB_3
);

  xor xor_1 (MSB_3, MSB, MSB_2);
  xor xor_2 (out_10, A, B);
  xor xor_3 (out_11, in_3, in_7);
  xor xor_4 (LSB_3, LSB, LSB_2);
endmodule

module not_4bits (
  input  in_1,
  input  in_2,
  input  in_3,
  input  in_4,
  output out_5,
  output out_6,
  output out_7,
  output out_8
);

  not not_1 (out_5, in_1);
  not not_2 (out_6, in_2);
  not not_3 (out_7, in_3);
  not not_4 (out_8, in_4);
endmodule

module comparador_4bits_otm (
  input  A3,
  input  A2,
  input  A1,
  input  A0,
  input  B3,
  input  B2,
  input  B1,
  input  B0,
  output Igual,
  output Mayor,
  output Menor
);

  wire restador_4bits_1_s1, restador_4bits_1_s2, restador_4bits_1_s3, restador_4bits_1_s4,
       restador_4bits_1_signo;

  restador_4bits restador_4bits_1 (
    .A3(A3), .A2(A2), .A1(A1), .A0(A0), .B3(B3), .B2(B2), .B1(B1), .B0(B0), .SIGNO(restador_4bits_1_signo),
    .S4(restador_4bits_1_s4), .S3(restador_4bits_1_s3), .S2(restador_4bits_1_s2), .S1(restador_4bits_1_s1));
  and and_1 (Igual, ~restador_4bits_1_s4, ~restador_4bits_1_s3, ~restador_4bits_1_s2, ~restador_4bits_1_s1);  // AND_Gate
  and and_2 (Mayor, ~Igual, restador_4bits_1_signo);  // AND_Gate
  and and_3 (Menor, ~Igual, ~restador_4bits_1_signo);  // AND_Gate

  // Notes on the sheet:
  //   A
  //   B
  //   A-B = 0 SON IGUALES
  //   A-B = POSITIVO --> A ES MAYOR A B
  //   A-B = NEGATIVO --> A ES MENOR QUE B
endmodule

module BCD_7SEGMENTOS_DERECHA (
  input  x0,
  input  x1,
  input  x2,
  input  x3,
  input  x4,
  output a,
  output b,
  output c,
  output d,
  output e,
  output f,
  output g
);

  wire and_1_out, and_2_out, and_3_out, and_4_out, and_5_out, and_6_out, and_7_out, and_8_out, and_9_out,
       and_10_out, and_11_out, and_12_out, and_13_out, and_14_out, and_15_out, and_16_out, and_17_out,
       and_18_out, and_19_out, and_20_out, and_21_out, and_22_out, and_23_out, and_24_out, and_25_out,
       and_26_out, and_27_out, and_28_out, and_29_out, and_30_out, and_31_out, and_32_out, and_33_out,
       and_34_out, and_35_out, and_36_out, and_37_out, and_38_out, and_39_out, and_40_out, and_41_out,
       and_42_out, and_43_out, and_44_out, and_45_out, and_46_out, and_47_out, and_48_out, and_49_out,
       and_50_out, and_51_out, and_52_out, not_1_out, not_2_out, not_3_out, not_4_out, not_5_out, not_6_out,
       not_7_out, not_8_out, not_9_out, not_10_out, not_11_out, not_12_out, not_13_out, not_14_out,
       not_15_out, not_16_out, not_17_out, not_18_out, not_19_out, not_20_out, not_21_out, not_22_out,
       not_23_out, not_24_out, not_25_out, not_26_out, not_27_out, not_28_out, not_29_out, not_30_out,
       not_31_out, not_32_out, not_33_out, not_34_out, not_35_out, not_36_out, not_37_out, not_38_out,
       not_39_out, not_40_out, not_41_out, not_42_out, not_43_out, not_44_out, not_45_out, not_46_out,
       not_47_out, not_48_out, not_49_out, not_50_out, not_51_out, not_52_out, not_53_out, not_54_out,
       not_55_out, not_56_out, not_57_out, not_58_out, not_59_out, not_60_out, not_61_out, not_62_out,
       not_63_out, not_64_out, not_65_out, not_66_out, not_67_out, not_68_out, not_69_out, not_70_out,
       not_71_out, not_72_out, not_73_out, not_74_out, not_75_out, not_76_out, not_77_out, not_78_out,
       not_79_out, not_80_out;

  not not_1 (not_1_out, x3);
  not not_2 (not_2_out, x4);
  not not_3 (not_3_out, x1);
  not not_4 (not_4_out, x2);
  not not_5 (not_5_out, x1);
  not not_6 (not_6_out, x0);
  not not_7 (not_7_out, x2);
  not not_8 (not_8_out, x3);
  not not_9 (not_9_out, x0);
  not not_10 (not_10_out, x2);
  not not_11 (not_11_out, x4);
  not not_12 (not_12_out, x2);
  not not_13 (not_13_out, x4);
  not not_14 (not_14_out, x3);
  not not_15 (not_15_out, x3);
  not not_16 (not_16_out, x3);
  not not_17 (not_17_out, x0);
  not not_18 (not_18_out, x1);
  not not_19 (not_19_out, x0);
  not not_20 (not_20_out, x1);
  not not_21 (not_21_out, x0);
  not not_22 (not_22_out, x1);
  not not_23 (not_23_out, x2);
  not not_24 (not_24_out, x2);
  not not_25 (not_25_out, x1);
  not not_26 (not_26_out, x3);
  not not_27 (not_27_out, x4);
  not not_28 (not_28_out, x1);
  not not_29 (not_29_out, x0);
  not not_30 (not_30_out, x3);
  not not_31 (not_31_out, x1);
  not not_32 (not_32_out, x0);
  not not_33 (not_33_out, x3);
  not not_34 (not_34_out, x2);
  not not_35 (not_35_out, x3);
  not not_36 (not_36_out, x0);
  not not_37 (not_37_out, x3);
  not not_38 (not_38_out, x4);
  not not_39 (not_39_out, x0);
  not not_40 (not_40_out, x2);
  not not_41 (not_41_out, x4);
  not not_42 (not_42_out, x1);
  not not_43 (not_43_out, x4);
  not not_44 (not_44_out, x0);
  not not_45 (not_45_out, x0);
  not not_46 (not_46_out, x3);
  not not_47 (not_47_out, x0);
  not not_48 (not_48_out, x3);
  not not_49 (not_49_out, x0);
  not not_50 (not_50_out, x2);
  not not_51 (not_51_out, x4);
  not not_52 (not_52_out, x0);
  not not_53 (not_53_out, x1);
  not not_54 (not_54_out, x0);
  not not_55 (not_55_out, x1);
  not not_56 (not_56_out, x1);
  not not_57 (not_57_out, x2);
  not not_58 (not_58_out, x4);
  not not_59 (not_59_out, x0);
  not not_60 (not_60_out, x1);
  not not_61 (not_61_out, x3);
  not not_62 (not_62_out, x2);
  not not_63 (not_63_out, x3);
  not not_64 (not_64_out, x0);
  not not_65 (not_65_out, x3);
  not not_66 (not_66_out, x4);
  not not_67 (not_67_out, x1);
  not not_68 (not_68_out, x3);
  not not_69 (not_69_out, x4);
  not not_70 (not_70_out, x1);
  not not_71 (not_71_out, x3);
  not not_72 (not_72_out, x4);
  not not_73 (not_73_out, x0);
  not not_74 (not_74_out, x3);
  not not_75 (not_75_out, x2);
  not not_76 (not_76_out, x3);
  not not_77 (not_77_out, x1);
  not not_78 (not_78_out, x4);
  not not_79 (not_79_out, x0);
  not not_80 (not_80_out, x2);
  and and_1 (and_1_out, x1, not_1_out);
  and and_2 (and_2_out, x0, x2, not_2_out);
  and and_3 (and_3_out, x0, x3, not_3_out);
  and and_4 (and_4_out, x1, x4, not_4_out);
  and and_5 (and_5_out, x2, x3, not_5_out);
  and and_6 (and_6_out, x2, x4, not_6_out);
  and and_7 (and_7_out, x4, not_7_out, not_8_out);
  and and_8 (and_8_out, not_9_out, not_10_out, not_11_out);
  and and_9 (and_9_out, x0, x1, x4);
  and and_10 (and_10_out, not_12_out, not_13_out);
  and and_11 (and_11_out, x0, x1, not_14_out);
  and and_12 (and_12_out, x0, x4, not_15_out);
  and and_13 (and_13_out, x1, x4, not_16_out);
  and and_14 (and_14_out, x2, x3, not_17_out);
  and and_15 (and_15_out, x2, x3, not_18_out);
  and and_16 (and_16_out, x2, not_19_out, not_20_out);
  and and_17 (and_17_out, x3, not_21_out, not_22_out);
  and and_18 (and_18_out, x3, x4);
  and and_19 (and_19_out, x3, not_23_out);
  and and_20 (and_20_out, x4, not_24_out);
  and and_21 (and_21_out, not_25_out, not_26_out);
  and and_22 (and_22_out, x1, x2, not_27_out);
  and and_23 (and_23_out, x0, x3, not_28_out);
  and and_24 (and_24_out, x1, x4, not_29_out);
  and and_25 (and_25_out, x1, x4, not_30_out);
  and and_26 (and_26_out, x2, x3, not_31_out);
  and and_27 (and_27_out, x1, not_32_out, not_33_out);
  and and_28 (and_28_out, x1, not_34_out, not_35_out);
  and and_29 (and_29_out, x4, not_36_out, not_37_out);
  and and_30 (and_30_out, x0, x2, x3, not_38_out);
  and and_31 (and_31_out, not_39_out, not_40_out, not_41_out);
  and and_32 (and_32_out, x0, x2, not_42_out, not_43_out);
  and and_33 (and_33_out, x1, x4, not_44_out);
  and and_34 (and_34_out, x1, not_45_out, not_46_out);
  and and_35 (and_35_out, x4, not_47_out, not_48_out);
  and and_36 (and_36_out, not_49_out, not_50_out, not_51_out);
  and and_37 (and_37_out, x2, x3, not_52_out, not_53_out);
  and and_38 (and_38_out, x1, x3, not_54_out);
  and and_39 (and_39_out, x3, x4, not_55_out);
  and and_40 (and_40_out, x3, not_56_out, not_57_out);
  and and_41 (and_41_out, x1, x2, x3, not_58_out);
  and and_42 (and_42_out, not_59_out, not_60_out, not_61_out);
  and and_43 (and_43_out, x1, x4, not_62_out, not_63_out);
  and and_44 (and_44_out, x2, not_64_out, not_65_out, not_66_out);
  and and_45 (and_45_out, x2, not_67_out, not_68_out, not_69_out);
  and and_46 (and_46_out, x3, not_70_out);
  and and_47 (and_47_out, x1, x4, not_71_out);
  and and_48 (and_48_out, x2, x3, not_72_out);
  and and_49 (and_49_out, x1, not_73_out, not_74_out);
  and and_50 (and_50_out, x1, not_75_out, not_76_out);
  and and_51 (and_51_out, x2, not_77_out, not_78_out);
  and and_52 (and_52_out, x4, not_79_out, not_80_out);
  or or_1 (a, and_1_out, and_2_out, and_3_out, and_4_out, and_5_out, and_6_out, and_7_out, and_8_out);
  or or_2 (b, and_9_out, and_10_out, and_11_out, and_12_out, and_13_out, and_14_out, and_15_out, and_16_out, and_17_out);
  or or_3 (c, x0, and_18_out, and_19_out, and_20_out, and_21_out, and_22_out);
  or or_4 (d, and_23_out, and_24_out, and_25_out, and_26_out, and_27_out, and_28_out, and_29_out, and_30_out, and_31_out, and_32_out);
  or or_5 (e, and_33_out, and_34_out, and_35_out, and_36_out, and_37_out);
  or or_6 (f, and_38_out, and_39_out, and_40_out, and_41_out, and_42_out, and_43_out, and_44_out, and_45_out);
  or or_7 (g, and_46_out, and_47_out, and_48_out, and_49_out, and_50_out, and_51_out, and_52_out);
endmodule

module BCD_7SEGMENTOS_IZQUIERDA (
  input  A4,
  input  A3,
  input  A2,
  input  A1,
  input  A0,
  output d,
  output g,
  output b,
  output e,
  output a,
  output c,
  output f
);

  wire and_2_out, and_3_out, and_5_out, and_6_out, and_7_out, comparador_4bits_otm_1_menor, D1, D2, D3,
       not_1_out, not_2_out, not_3_out, not_4_out, not_5_out, not_6_out, not_7_out;

  not not_1 (not_1_out, 1'b1);
  comparador_4bits_otm comparador_4bits_otm_1 (
    .A3(A3), .A2(A2), .A1(A1), .A0(A0), .B3(1'b1), .B2(not_1_out), .B1(1'b1), .B0(not_1_out),
    .Menor(comparador_4bits_otm_1_menor));  // open: Igual, Mayor
  not not_2 (not_2_out, A3);
  not not_3 (not_3_out, A2);
  not not_4 (not_4_out, A4);
  and and_1 (f, ~A4, comparador_4bits_otm_1_menor);  // AND_Gate
  and and_2 (and_2_out, A4, not_2_out, not_3_out);
  or or_1 (D1, and_2_out, and_3_out);
  and and_3 (and_3_out, not_4_out, A3, A2);
  or or_2 (a, D3, f, D2);
  or or_3 (b, f, D1, D2, D3);
  or or_4 (d, f, D2, D3);
  or or_5 (c, D1, f, D3);
  or or_6 (e, f, D2);
  and and_4 (D3, ~A0, A1, A2, A3, A4);  // AND_Gate
  not not_5 (not_5_out, A3);
  not not_6 (not_6_out, A2);
  not not_7 (not_7_out, A1);
  and and_5 (and_5_out, A4, not_5_out, A2);
  and and_6 (and_6_out, A4, A3, not_6_out);
  and and_7 (and_7_out, A4, A3, A2, not_7_out);
  or or_7 (g, D2, D3);
  or or_8 (D2, and_5_out, and_6_out, and_7_out);

  // Other names for the same wires on the sheet: D0 = f

  // Notes on the sheet:
  //   Si el numero A es menor a 10 en binario (1010)
  //   Decenas = 0
  //   Decenas = 1
  //   Si el numero A es menor a 20 pero mayor o igual que 10 en decimal
  //   Decenas = 3
  //   Si el numero A es exactamente igual a 30 porque dos numeros de 4 bits sumados no pueden dar un numero mayor a 30
  //   Si el numero A es menor a 30 pero mayor o igual que 20 en decimal
  //   Decenas = 2
endmodule

module Decenas2 (
  input  A0,
  input  A1,
  input  A2,
  input  A3,
  input  A4,
  output D2
);

  wire and_1_out, and_2_out, and_3_out, not_1_out, not_2_out, not_3_out;

  not not_1 (not_1_out, A3);
  not not_2 (not_2_out, A2);
  not not_3 (not_3_out, A1);
  and and_1 (and_1_out, A4, not_1_out, A2);
  and and_2 (and_2_out, A4, A3, not_2_out);
  and and_3 (and_3_out, A4, A3, A2, not_3_out);
  or or_1 (D2, and_1_out, and_2_out, and_3_out);
endmodule
